# Fritzing sketch spideruino_programming (saved by Fritzing 0.9.3b)
breadboards: 1

parts:
  U1 = ESP8266 WiFi Module [part_number=ESP8266]
  J1 = Basic Servo
  J2 = Basic Servo
  J3 = Basic Servo
  Part1 = FTDI Basic Programmer
  C1 = Ceramic Capacitor [capacitance=100nF package="200 mil [THT, multilayer]"]
  R1 = Resistor [tolerance=±5% resistance=330 package="2010 [SMD]"]
  R2 = Resistor [tolerance=±5% resistance=1k package="2010 [SMD]"]

nets:
  GND: U1.IO0, U1.IO15, U1.GND, J1.gnd, J2.gnd, J3.gnd, Part1.GND, C1.1
  N1: U1.IO2, J1.pulse
  N2: U1.D2, J2.pulse
  N3: U1.CLK, J3.pulse
  N4: U1.D0, C1.0, R2.Pin_0
  N5: U1.IO13, R1.Pin_1
  N6: U1.TX, Part1.RXI
  N7: U1.RX, Part1.TXO
  VCC: U1.3.3V, J1.vcc, J2.vcc, J3.vcc, Part1.POWER, R1.Pin_0, R2.Pin_1

notes:
  Left, Mid, Right legs
